// Logisim project bonkpu.circ as structural Verilog: 4 circuits, main circuit main
module main (
);

  wire AI, AO, BI, BO, button_1_out, button_2_out, CE, CI, CLK, clock_1_out, CO, dipswitch_1_p2,
       dipswitch_1_p3, EO, FI, HLT, IE, II, MI, MS0, not_1_out, RI, RO, SO, SU, XI, XM, XO;
  wire [1:0] STACK_MODE;
  wire [2:0] FLAGS, nor_1_out;
  wire [3:0] MICHAELSTEP_q;
  wire [5:5] michaelcode_a_data;
  wire [7:0] A_REG_q, adder_1_out, B_REG_q, MAR_q, MEM_dout, michaelcode_b_data, multiplexer_1_out,
       multiplexer_2_out, OP_REG_q, stack_pointer_1_out_bus, X_REG_q, xor_1_out;

  Counter #(.max('hf), .width(4)) MICHAELSTEP (
    .load(IE), .clk(not_1_out), .D(4'b0000), .Q(MICHAELSTEP_q));  // open: clr, up, count, carry
  not not_1 (not_1_out, CLK);
  Register MAR (.D(stack_pointer_1_out_bus), .en(MI), .clk(CLK), .Q(MAR_q));  // open: clr
  Register OP_REG (.D(stack_pointer_1_out_bus), .en(II), .clk(CLK), .Q(OP_REG_q));  // open: clr
  RAM #(.enables("line")) MEM (.addr(MAR_q), .we(RI), .clk(CLK), .din(stack_pointer_1_out_bus), .dout(MEM_dout));
  Comparator #(.mode("unsigned"), .width(4)) comparator_1 (.a(MICHAELSTEP_q), .b(4'b0000), .eq(MS0));  // open: gt, lt
  // Probe on FLAGS
  // Probe on OP_REG_q
  // Probe on MICHAELSTEP_q
  ROM #(.addrWidth(15)) michaelcode_a (
    .addr({FLAGS, OP_REG_q, MICHAELSTEP_q}), .data({IE, CE, michaelcode_a_data[5], XM, SU, FI, STACK_MODE}));
  stack_pointer stack_pointer_1 (.LO(SO), .CLK(CLK), .MODE(STACK_MODE), .out_bus(stack_pointer_1_out_bus));
  program_counter program_counter_1 (
    .CE(CE), .CLK(CLK), .I(CI), .O(CO), .bus_in(stack_pointer_1_out_bus), .bus_out(stack_pointer_1_out_bus));
  LedBar ledbar_1 (
    .led0(stack_pointer_1_out_bus[7]), .led1(stack_pointer_1_out_bus[6]), .led2(stack_pointer_1_out_bus[5]),
    .led3(stack_pointer_1_out_bus[4]), .led4(stack_pointer_1_out_bus[3]), .led5(stack_pointer_1_out_bus[2]),
    .led6(stack_pointer_1_out_bus[1]), .led7(stack_pointer_1_out_bus[0]));
  Register X_REG (.D(stack_pointer_1_out_bus), .en(XI), .clk(CLK), .Q(X_REG_q));  // open: clr
  Pull_Resistor pull_resistor_1 (.node(stack_pointer_1_out_bus));
  Register A_REG (.D(stack_pointer_1_out_bus), .en(AI), .clk(CLK), .Q(A_REG_q));  // open: clr
  assign stack_pointer_1_out_bus = AO ? A_REG_q : 8'bz;  // Controlled_Buffer controlled_buffer_1
  assign stack_pointer_1_out_bus = EO ? adder_1_out : 8'bz;  // Controlled_Buffer EO_GATE
  assign stack_pointer_1_out_bus = RO ? MEM_dout : 8'bz;  // Controlled_Buffer controlled_buffer_2
  Register B_REG (.D(stack_pointer_1_out_bus), .en(BI), .clk(CLK), .Q(B_REG_q));  // open: clr
  LedBar #(.matrixcols(16)) ledbar_2 (
    .led0(IE), .led1(CE), .led2(michaelcode_a_data[5]), .led3(XM), .led4(SU), .led5(FI),
    .led6(STACK_MODE[1]), .led7(STACK_MODE[0]), .led8(michaelcode_b_data[7]), .led9(michaelcode_b_data[6]),
    .led10(michaelcode_b_data[5]), .led11(michaelcode_b_data[4]), .led12(michaelcode_b_data[3]),
    .led13(michaelcode_b_data[2]), .led14(michaelcode_b_data[1]), .led15(michaelcode_b_data[0]));
  ROM #(.addrWidth(15)) michaelcode_b (.addr({FLAGS, OP_REG_q, MICHAELSTEP_q}), .data(michaelcode_b_data));
  assign stack_pointer_1_out_bus = XO ? X_REG_q : 8'bz;  // Controlled_Buffer controlled_buffer_3
  assign stack_pointer_1_out_bus = BO ? B_REG_q : 8'bz;  // Controlled_Buffer B_GATE
  // Probe on X_REG_q
  // Probe on X_REG_q
  // Probe on A_REG_q
  // Probe on A_REG_q
  Multiplexer #(.width(8)) multiplexer_1 (.in0({8{1'b0}}), .in1({8{1'b1}}), .out(multiplexer_1_out), .sel(SU));
  // Probe on B_REG_q
  // Probe on B_REG_q
  Multiplexer #(.width(8)) multiplexer_2 (.in0(A_REG_q), .in1(X_REG_q), .out(multiplexer_2_out), .sel(XM));
  assign xor_1_out = multiplexer_1_out ^ B_REG_q;  // XOR_Gate xor_1, 8 bits wide
  // DipSwitch #(.number(2)) dipswitch_1: pin names not known; wires that end beside it: multiplexer_2_out, dipswitch_1_p2, dipswitch_1_p3
  Button button_1 (.out(button_1_out));
  Button button_2 (.out(button_2_out));
  Clock clock_1 (.out(clock_1_out));
  Adder adder_1 (.a(multiplexer_2_out), .b(xor_1_out), .out(adder_1_out), .cin(SU), .cout(nor_1_out[2]));
  nor nor_1 (nor_1_out[0], adder_1_out[0], adder_1_out[1], adder_1_out[2], adder_1_out[3], adder_1_out[4], adder_1_out[5], adder_1_out[6], adder_1_out[7]);
  // Probe on adder_1_out
  // Probe on adder_1_out
  clk_module clk_module_1 (
    .EUSTEP(dipswitch_1_p2), .ESTEP(dipswitch_1_p3), .CLK_IN(clock_1_out), .USTEP(button_1_out),
    .STEP(button_2_out), .HLT(HLT), .MS0(MS0), .CLK(CLK));
  Decoder #(.enable("false"), .select(4)) decoder_1 (
    .out1(RO), .out2(AO), .out3(BO), .out4(EO), .out5(CO), .out6(SO), .out7(XO), .out15(HLT),
    .sel(michaelcode_b_data[3:0]));  // open: out0, out8, out9, out10, out11, out12, out13, out14
  Decoder #(.enable("false"), .select(4)) decoder_2 (
    .out1(RI), .out2(AI), .out3(BI), .out4(II), .out5(CI), .out6(MI), .out7(XI), .sel(michaelcode_b_data[7:4]));  // open: out0, out8, out9, out10, out11, out12, out13, out14, out15
  Register #(.width(3)) FLAG_REG (
    .D({nor_1_out[2], adder_1_out[7], nor_1_out[0]}), .en(FI), .clk(CLK), .Q(FLAGS));  // open: clr
  // Probe on michaelcode_b_data[3:0]
  // Probe on michaelcode_b_data[7:4]
  LedBar #(.matrixcols(3)) ledbar_3 (.led0(FLAGS[2]), .led1(FLAGS[1]), .led2(FLAGS[0]));

  // Notes on the sheet:
  //   contents of michaelcode_a (hex, n*v repeats v):
  //   0 c0 15*0 40 0 80 13*0 40 0 c0 13*0 40 0 40 0 10 80 10*0 40 0 40 0 10 0 0 40 10 80 6*0 40 0 40 80
  //   12*0 40 0 40 0 10 80 10*0 40 0 40 84 12*0 40 0 40 0 10 0 84 9*0 40 0 40 8c 12*0 40 0 40 0 10 0 8c
  //   9*0 40 0 40 8c 12*0 40 0 c0 13*0 40 c0 14*0 40 0 c0 13*0 40 c0 14*0 40 0 c0 13*0 40 c0 14*0 40 0 c0
  //   13*0 40 81 14*0 40 83 14*0 40 82 14*0 40 0 83 13*0 40 0 40 0 83 11*0 40 2 0 80 12*0 40 0 3 0 c0 11*0
  //   40 2 0 0 c0 11*0 40 80 14*0 c0 15*0 c0 15*0 c0 15*0 c0 15*0 c0 15*0 c0 15*0 c0 15*0 c0 15*0 c0 15*0
  //   c0 15*0 c0 15*0 c0 15*0 c0 15*0 c0 15*0 c0 15*0 c0 15*0 c0 15*0 c0 15*0 c0 15*0 c0 15*0 c0 15*0 c0
  //   15*0 c0 15*0 c0 15*0 c0 15*0 c0 15*0 c0 15*0 c0 15*0 c0 15*0 c0 15*0 c0 15*0 c0 15*0 c0 15*0 c0 15*0
  //   c0 15*0 c0 15*0 c0 15*0 c0 15*0 c0 15*0 c0 15*0 c0 15*0 c0 15*0 c0 15*0 c0 15*0 c0 15*0 c0 15*0 c0
  //   15*0 c0 15*0 c0 15*0 c0 15*0 c0 15*0 c0 15*0 c0 15*0 c0 15*0 c0 15*0 c0 15*0 c0 15*0 c0 15*0 c0 15*0
  //   c0 15*0 c0 15*0 c0 15*0 c0 15*0 c0 15*0 c0 15*0 c0 15*0 c0 15*0 c0 15*0 c0 15*0 c0 15*0 c0 15*0 c0
  //   15*0 c0 15*0 c0 15*0 c0 15*0 c0 15*0 c0 15*0 c0 15*0 c0 15*0 c0 15*0 c0 15*0 c0 15*0 c0 15*0 c0 15*0
  //   c0 15*0 c0 15*0 c0 15*0 c0 15*0 c0 15*0 c0 15*0 c0 15*0 c0 15*0 c0 15*0 c0 15*0 c0 15*0 c0 15*0 c0
  //   15*0 c0 15*0 c0 15*0 c0 15*0 c0 15*0 c0 15*0 c0 15*0 c0 15*0 c0 15*0 c0 15*0 c0 15*0 c0 15*0 c0 15*0
  //   c0 15*0 c0 15*0 c0 15*0 c0 15*0 c0 15*0 c0 15*0 c0 15*0 c0 15*0 c0 15*0 c0 15*0 c0 15*0 c0 15*0 c0
  //   15*0 c0 15*0 c0 15*0 c0 15*0 c0 15*0 c0 15*0 c0 15*0 c0 15*0 c0 15*0 c0 15*0 c0 15*0 c0 15*0 c0 15*0
  //   c0 15*0 c0 15*0 c0 15*0 c0 15*0 c0 15*0 c0 15*0 c0 15*0 c0 15*0 c0 15*0 c0 15*0 c0 15*0 c0 15*0 c0
  //   15*0 c0 15*0 c0 15*0 c0 15*0 c0 15*0 c0 15*0 c0 15*0 c0 15*0 c0 15*0 c0 15*0 c0 15*0 c0 15*0 c0 15*0
  //   c0 15*0 c0 15*0 c0 15*0 c0 15*0 c0 15*0 c0 15*0 c0 15*0 c0 15*0 c0 15*0 c0 15*0 c0 15*0 c0 15*0 c0
  //   15*0 c0 15*0 c0 15*0 c0 15*0 c0 15*0 c0 15*0 c0 15*0 c0 15*0 c0 15*0 c0 15*0 c0 15*0 c0 15*0 c0 15*0
  //   c0 15*0 c0 15*0 c0 15*0 c0 15*0 c0 15*0 c0 15*0 c0 15*0 c0 15*0 c0 15*0 c0 15*0 c0 15*0 c0 15*0 c0
  //   15*0 c0 15*0 c0 15*0 c0 15*0 c0 15*0 c0 15*0 c0 15*0 c0 15*0 c0 15*0 c0 15*0 c0 15*0 c0 15*0 c0 15*0
  //   c0 15*0 c0 15*0 c0 15*0 c0 15*0 c0 15*0 c0 15*0 c0 15*0 c0 15*0 c0 15*0 c0 15*0 c0 15*0 c0 15*0 c0
  //   15*0 c0 15*0 c0 15*0 c0 15*0 c0 15*0 c0 15*0 c0 15*0 c0 15*0 40 0 80 13*0 40 0 c0 13*0 40 0 40 0 10
  //   80 10*0 40 0 40 0 10 0 0 40 10 80 6*0 40 0 40 80 12*0 40 0 40 0 10 80 10*0 40 0 40 84 12*0 40 0 40 0
  //   10 0 84 9*0 40 0 40 8c 12*0 40 0 40 0 10 0 8c 9*0 40 0 40 8c 12*0 40 0 c0 13*0 40 0 c0 13*0 40 c0
  //   14*0 40 c0 14*0 40 0 c0 13*0 40 c0 14*0 40 0 c0 13*0 40 81 14*0 40 83 14*0 40 82 14*0 40 0 83 13*0
  //   40 0 40 0 83 11*0 40 2 0 80 12*0 40 0 3 0 c0 11*0 40 2 0 0 c0 11*0 40 80 14*0 c0 15*0 c0 15*0 c0
  //   15*0 c0 15*0 c0 15*0 c0 15*0 c0 15*0 c0 15*0 c0 15*0 c0 15*0 c0 15*0 c0 15*0 c0 15*0 c0 15*0 c0 15*0
  //   c0 15*0 c0 15*0 c0 15*0 c0 15*0 c0 15*0 c0 15*0 c0 15*0 c0 15*0 c0 15*0 c0 15*0 c0 15*0 c0 15*0 c0
  //   15*0 c0 15*0 c0 15*0 c0 15*0 c0 15*0 c0 15*0 c0 15*0 c0 15*0 c0 15*0 c0 15*0 c0 15*0 c0 15*0 c0 15*0
  //   c0 15*0 c0 15*0 c0 15*0 c0 15*0 c0 15*0 c0 15*0 c0 15*0 c0 15*0 c0 15*0 c0 15*0 c0 15*0 c0 15*0 c0
  //   15*0 c0 15*0 c0 15*0 c0 15*0 c0 15*0 c0 15*0 c0 15*0 c0 15*0 c0 15*0 c0 15*0 c0 15*0 c0 15*0 c0 15*0
  //   c0 15*0 c0 15*0 c0 15*0 c0 15*0 c0 15*0 c0 15*0 c0 15*0 c0 15*0 c0 15*0 c0 15*0 c0 15*0 c0 15*0 c0
  //   15*0 c0 15*0 c0 15*0 c0 15*0 c0 15*0 c0 15*0 c0 15*0 c0 15*0 c0 15*0 c0 15*0 c0 15*0 c0 15*0 c0 15*0
  //   c0 15*0 c0 15*0 c0 15*0 c0 15*0 c0 15*0 c0 15*0 c0 15*0 c0 15*0 c0 15*0 c0 15*0 c0 15*0 c0 15*0 c0
  //   15*0 c0 15*0 c0 15*0 c0 15*0 c0 15*0 c0 15*0 c0 15*0 c0 15*0 c0 15*0 c0 15*0 c0 15*0 c0 15*0 c0 15*0
  //   c0 15*0 c0 15*0 c0 15*0 c0 15*0 c0 15*0 c0 15*0 c0 15*0 c0 15*0 c0 15*0 c0 15*0 c0 15*0 c0 15*0 c0
  //   15*0 c0 15*0 c0 15*0 c0 15*0 c0 15*0 c0 15*0 c0 15*0 c0 15*0 c0 15*0 c0 15*0 c0 15*0 c0 15*0 c0 15*0
  //   c0 15*0 c0 15*0 c0 15*0 c0 15*0 c0 15*0 c0 15*0 c0 15*0 c0 15*0 c0 15*0 c0 15*0 c0 15*0 c0 15*0 c0
  //   15*0 c0 15*0 c0 15*0 c0 15*0 c0 15*0 c0 15*0 c0 15*0 c0 15*0 c0 15*0 c0 15*0 c0 15*0 c0 15*0 c0 15*0
  //   c0 15*0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
  //   contents of michaelcode_b (hex, n*v repeats v):
  //   65 41 14*0 65 41 62 21 12*0 65 41 65 21 12*0 65 41 65 71 36 64 21 9*0 65 41 65 71 36 64 71 65 31 64
  //   21 5*0 65 41 65 61 12 11*0 65 41 65 71 36 64 12 9*0 65 41 65 31 24 11*0 65 41 65 71 36 64 31 24 8*0
  //   65 41 65 31 24 11*0 65 41 65 71 36 64 31 24 8*0 65 41 65 31 12*0 65 41 65 51 12*0 65 41 14*0 65 41
  //   65 51 12*0 65 41 14*0 65 41 65 51 12*0 65 41 14*0 65 41 65 51 12*0 65 41 14*0 65 41 14*0 65 41 14*0
  //   65 41 66 12 12*0 65 41 65 31 66 13 10*0 65 41 0 66 21 11*0 65 41 66 15 65 51 10*0 65 41 0 66 51 11*0
  //   65 41 f 13*0 65 41 14*0 65 41 14*0 65 41 14*0 65 41 14*0 65 41 14*0 65 41 14*0 65 41 14*0 65 41 14*0
  //   65 41 14*0 65 41 14*0 65 41 14*0 65 41 14*0 65 41 14*0 65 41 14*0 65 41 14*0 65 41 14*0 65 41 14*0
  //   65 41 14*0 65 41 14*0 65 41 14*0 65 41 14*0 65 41 14*0 65 41 14*0 65 41 14*0 65 41 14*0 65 41 14*0
  //   65 41 14*0 65 41 14*0 65 41 14*0 65 41 14*0 65 41 14*0 65 41 14*0 65 41 14*0 65 41 14*0 65 41 14*0
  //   65 41 14*0 65 41 14*0 65 41 14*0 65 41 14*0 65 41 14*0 65 41 14*0 65 41 14*0 65 41 14*0 65 41 14*0
  //   65 41 14*0 65 41 14*0 65 41 14*0 65 41 14*0 65 41 14*0 65 41 14*0 65 41 14*0 65 41 14*0 65 41 14*0
  //   65 41 14*0 65 41 14*0 65 41 14*0 65 41 14*0 65 41 14*0 65 41 14*0 65 41 14*0 65 41 14*0 65 41 14*0
  //   65 41 14*0 65 41 14*0 65 41 14*0 65 41 14*0 65 41 14*0 65 41 14*0 65 41 14*0 65 41 14*0 65 41 14*0
  //   65 41 14*0 65 41 14*0 65 41 14*0 65 41 14*0 65 41 14*0 65 41 14*0 65 41 14*0 65 41 14*0 65 41 14*0
  //   65 41 14*0 65 41 14*0 65 41 14*0 65 41 14*0 65 41 14*0 65 41 14*0 65 41 14*0 65 41 14*0 65 41 14*0
  //   65 41 14*0 65 41 14*0 65 41 14*0 65 41 14*0 65 41 14*0 65 41 14*0 65 41 14*0 65 41 14*0 65 41 14*0
  //   65 41 14*0 65 41 14*0 65 41 14*0 65 41 14*0 65 41 14*0 65 41 14*0 65 41 14*0 65 41 14*0 65 41 14*0
  //   65 41 14*0 65 41 14*0 65 41 14*0 65 41 14*0 65 41 14*0 65 41 14*0 65 41 14*0 65 41 14*0 65 41 14*0
  //   65 41 14*0 65 41 14*0 65 41 14*0 65 41 14*0 65 41 14*0 65 41 14*0 65 41 14*0 65 41 14*0 65 41 14*0
  //   65 41 14*0 65 41 14*0 65 41 14*0 65 41 14*0 65 41 14*0 65 41 14*0 65 41 14*0 65 41 14*0 65 41 14*0
  //   65 41 14*0 65 41 14*0 65 41 14*0 65 41 14*0 65 41 14*0 65 41 14*0 65 41 14*0 65 41 14*0 65 41 14*0
  //   65 41 14*0 65 41 14*0 65 41 14*0 65 41 14*0 65 41 14*0 65 41 14*0 65 41 14*0 65 41 14*0 65 41 14*0
  //   65 41 14*0 65 41 14*0 65 41 14*0 65 41 14*0 65 41 14*0 65 41 14*0 65 41 14*0 65 41 14*0 65 41 14*0
  //   65 41 14*0 65 41 14*0 65 41 14*0 65 41 14*0 65 41 14*0 65 41 14*0 65 41 14*0 65 41 14*0 65 41 14*0
  //   65 41 14*0 65 41 14*0 65 41 14*0 65 41 14*0 65 41 14*0 65 41 14*0 65 41 14*0 65 41 14*0 65 41 14*0
  //   65 41 14*0 65 41 14*0 65 41 14*0 65 41 14*0 65 41 14*0 65 41 14*0 65 41 14*0 65 41 14*0 65 41 14*0
  //   65 41 14*0 65 41 14*0 65 41 14*0 65 41 14*0 65 41 14*0 65 41 14*0 65 41 14*0 65 41 14*0 65 41 14*0
  //   65 41 14*0 65 41 14*0 65 41 14*0 65 41 14*0 65 41 14*0 65 41 14*0 65 41 14*0 65 41 14*0 65 41 14*0
  //   65 41 14*0 65 41 14*0 65 41 14*0 65 41 14*0 65 41 14*0 65 41 14*0 65 41 14*0 65 41 14*0 65 41 14*0
  //   65 41 14*0 65 41 14*0 65 41 14*0 65 41 14*0 65 41 14*0 65 41 14*0 65 41 14*0 65 41 14*0 65 41 14*0
  //   65 41 14*0 65 41 14*0 65 41 14*0 65 41 14*0 65 41 14*0 65 41 62 21 12*0 65 41 65 21 12*0 65 41 65 71
  //   36 64 21 9*0 65 41 65 71 36 64 71 65 31 64 21 5*0 65 41 65 61 12 11*0 65 41 65 71 36 64 12 9*0 65 41
  //   65 31 24 11*0 65 41 65 71 36 64 31 24 8*0 65 41 65 31 24 11*0 65 41 65 71 36 64 31 24 8*0 65 41 65
  //   31 12*0 65 41 65 51 12*0 65 41 65 51 12*0 65 41 14*0 65 41 14*0 65 41 65 51 12*0 65 41 14*0 65 41 65
  //   51 12*0 65 41 14*0 65 41 14*0 65 41 14*0 65 41 66 12 12*0 65 41 65 31 66 13 10*0 65 41 0 66 21 11*0
  //   65 41 66 15 65 51 10*0 65 41 0 66 51 11*0 65 41 f 13*0 65 41 14*0 65 41 14*0 65 41 14*0 65 41 14*0
  //   65 41 14*0 65 41 14*0 65 41 14*0 65 41 14*0 65 41 14*0 65 41 14*0 65 41 14*0 65 41 14*0 65 41 14*0
  //   65 41 14*0 65 41 14*0 65 41 14*0 65 41 14*0 65 41 14*0 65 41 14*0 65 41 14*0 65 41 14*0 65 41 14*0
  //   65 41 14*0 65 41 14*0 65 41 14*0 65 41 14*0 65 41 14*0 65 41 14*0 65 41 14*0 65 41 14*0 65 41 14*0
  //   65 41 14*0 65 41 14*0 65 41 14*0 65 41 14*0 65 41 14*0 65 41 14*0 65 41 14*0 65 41 14*0 65 41 14*0
  //   65 41 14*0 65 41 14*0 65 4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
endmodule

module stack_pointer (
  input  CLK,
  input  [1:0] MODE,
  input  LO,
  output [7:0] out_bus
);

  wire decoder_1_out0, decoder_1_out1, decoder_1_out2, decoder_1_out3, or_1_out;
  wire [7:0] counter_1_q;

  Decoder #(.enable("false"), .select(2)) decoder_1 (
    .out0(decoder_1_out0), .out1(decoder_1_out1), .out2(decoder_1_out2), .out3(decoder_1_out3), .sel(MODE));
  // NoConnect on decoder_1_out0
  LED INC (.in(decoder_1_out2));
  LED DEC (.in(decoder_1_out3));
  LED LOAD (.in(decoder_1_out1));
  or or_1 (or_1_out, decoder_1_out1, decoder_1_out2, decoder_1_out3);
  Counter counter_1 (
    .load(decoder_1_out1), .up(decoder_1_out2), .count(or_1_out), .clk(CLK), .D({8{1'b1}}), .Q(counter_1_q));  // open: clr, carry
  assign out_bus = LO ? counter_1_q : 8'bz;  // Controlled_Buffer controlled_buffer_1
endmodule

module program_counter (
  input  I,
  input  CE,
  input  CLK,
  input  O,
  input  [7:0] bus_in,
  output [7:0] bus_out
);

  wire or_1_out;
  wire [7:0] C_q;

  or or_1 (or_1_out, I, CE);
  Counter C (.load(I), .count(or_1_out), .clk(CLK), .D(bus_in), .Q(C_q));  // open: clr, up, carry
  assign bus_out = O ? C_q : 8'bz;  // Controlled_Buffer controlled_buffer_1
endmodule

module clk_module (
  input  EUSTEP,
  input  ESTEP,
  input  USTEP,
  input  STEP,
  input  CLK_IN,
  input  HLT,
  input  MS0,
  output CLK
);

  wire and_1_out, and_2_out, nor_1_out, not_1_out, xor_1_out;

  not not_1 (not_1_out, EUSTEP);
  xor xor_1 (xor_1_out, STEP, ESTEP);
  and and_1 (and_1_out, MS0, xor_1_out);
  nor nor_1 (nor_1_out, HLT, and_1_out);
  Multiplexer multiplexer_1 (.in0(USTEP), .in1(and_2_out), .out(CLK), .sel(not_1_out));
  and and_2 (and_2_out, CLK_IN, nor_1_out);
endmodule
